# Fritzing sketch Prototype PCB Soldering Planning (saved by Fritzing 1.0.4)
circuit board: 8.46667cm x 5.64444cm
breadboards: 1

parts:
  Part1 = Arduino Nano (Rev3.0)
  J1 = female pin header, 8 pins [form="♀ (female)"]
  J2 = female pin header, 5 pins [form="♀ (female)"]
  J3 = female pin header, 24 pins [form="♀ (female)"]
  J4 = female pin header, 24 pins [form="♀ (female)"]  # not connected
  J5 = female pin header, 10 pins [form="♀ (female)"]  # not connected
  J6 = female pin header, 10 pins [form="♀ (female)"]  # not connected
  VCC1 = Battery [internal_resistance=0.1Ω]
  D1 = Rectifier Diode [part_number=1N4001 package="300 mil [THT]"]
  VCC2 = Battery [internal_resistance=0.1Ω]
  J7 = female pin header, 7 pins [form="♀ (female)"]

nets:
  N1: Part1.D10, J2.pin4
  N2: Part1.D11/MOSI, J2.pin3
  N3: Part1.VIN, D1.cathode
  N4: Part1.GND, J1.pin2, J2.pin2, VCC1.-
  N5: Part1.5V, J1.pin1, J2.pin1
  N6: Part1.A5, J1.pin3
  N7: Part1.A4, J1.pin4
  N8: Part1.D13/SCK, J2.pin5
  N9: J3.pin13, J7.pin1
  N10: J3.pin14, J7.pin2
  N11: J3.pin15, J7.pin3
  N12: J3.pin16, J7.pin4
  N13: J3.pin17, J7.pin5
  N14: J3.pin18, J7.pin6
  N15: J3.pin19, J7.pin7
  N16: VCC1.+, VCC2.+
  N17: D1.anode, VCC2.-
